# Fritzing sketch Datalogger (saved by Fritzing 0.8.7b)
circuit board: 8.46667cm x 5.64444cm

parts:
  Part1 = Arduino Uno (Rev3)
  ZS-042_RTC1 = ZS-042 RTC Module
  SD_card_module1 = SD Card Module
  U1 = GAS_SENSOR [package=mq-3]

nets:
  N1: Part1.A4/SDA, ZS-042_RTC1.SDA
  N2: Part1.A5/SCL, ZS-042_RTC1.SCL
  N3: Part1.D10_PWM/SS, SD_card_module1.CS
  N4: Part1.D11_PWM/MOSI, SD_card_module1.MOSI
  N5: Part1.D12/MISO, SD_card_module1.MISO
  N6: Part1.D13/SCK, SD_card_module1.SCK
  N7: Part1.3V3, SD_card_module1.+5
  5V: Part1.5V, ZS-042_RTC1.VCC, U1.B1
  GND: Part1.GND, ZS-042_RTC1.GND, SD_card_module1.GND, U1.A1

custom parts:
  SD Card Module: SD Card Module Slot Socket Reader For Arduino ARM MCU
